# Fritzing sketch PowerSwitch (saved by Fritzing 0.7.11b)

parts:
  Arduino1 = Arduino
  R3 = Resistor [tolerance=±5% resistance=220 package=THT]
  LED1 = RGB LED (com. cathode, rgb) [package="5 mm [THT]"]
  C1 = Electrolytic Capacitor [capacitance=10µF package="100 mil [THT, electrolytic]"]
  R6 = Resistor [tolerance=±5% resistance=220 package=THT]
  R7 = Resistor [tolerance=±5% resistance=220 package=THT]
  R8 = Resistor [tolerance=±5% resistance=20k package=THT]
  R9 = Resistor [tolerance=±5% resistance=10k package=THT]
  K1 = Relay [part_number=FRS1B-S package=THT]
  J1 = screw terminal, 3 pins
  U1 = mystery part, 3 pins [chip_label=?]

nets:
  N1: Arduino1.GND, LED1.red_anode, R9.Pin_0, U1.pin2
  N2: Arduino1.D5, U1.pin3
  N3: Arduino1.D4, R7.Pin_1
  N4: Arduino1.D3, R6.Pin_1
  N5: Arduino1.D2, R3.Pin_1
  N6: Arduino1.RST, C1.+
  N7: Arduino1.+5V, U1.pin1
  N8: Arduino1.VIN, R8.Pin_0
  N9: Arduino1.A0, R9.Pin_1
  N10: K1.A, J1.pin3
  N11: K1.C1, K1.C2, J1.pin2
  N12: K1.B, J1.pin1

notes:
  USB
  (connect to PC)
  Power Adapter
  (connect to extension cord with switch button)
  Relay
  Module (powers PC)
